# Fritzing sketch project1 (saved by Fritzing 0.9.4)
breadboards: 1

parts:
  DHT1 = DHT11 Humitidy and Temperature Sensor
  Part1 = Arduino Uno (Rev3)
  R1 = Resistor [tolerance=±5% resistance=10k package=THT]

nets:
  VDD: DHT1.VDD, Part1.5V, R1.Pin_0
  N1: DHT1.DATA, Part1.D2, R1.Pin_1
  GND: DHT1.GND, Part1.GND

custom parts:
  DHT11 Humitidy and Temperature Sensor: DHT11 Humidity and Temperature Sensor
