# Fritzing sketch project1_2 (saved by Fritzing 0.9.4)

parts:
  DHT11_1 = DHT11 module
  Part1 = Arduino Uno (Rev3)

nets:
  VCC: DHT11_1.VCC, Part1.5V
  GND: DHT11_1.GND, Part1.GND
  N1: DHT11_1.DATA, Part1.D2

custom parts:
  DHT11 module: DHT11 black pcb module
